// Logisim project gerador de paridade impar.circ as structural Verilog: 1 circuit, main circuit main
module main (
  input  A,
  input  B,
  input  C,
  input  D,
  output out_5,
  output out_6,
  output out_7,
  output out_8,
  output out_9
);

  wire xor_1_out, xor_2_out;

  xor xor_1 (xor_1_out, A, B);
  xor xor_2 (xor_2_out, C, D);
  xnor xnor_1 (out_5, xor_1_out, xor_2_out);

  assign out_6 = D;
  assign out_7 = C;
  assign out_8 = B;
  assign out_9 = A;
endmodule
